// Logisim project 1 лаб(2в) .circ as structural Verilog: 3 circuits, main circuit 1
module _1 (
  input  x5,
  input  x4,
  input  x3,
  input  x2,
  input  x1,
  output y
);

  wire and_1_out, and_2_out, and_3_out, and_4_out, and_5_out, and_6_out, and_7_out, and_8_out, and_9_out,
       and_10_out, not_1_out, not_2_out, not_3_out, not_4_out, not_5_out, not_6_out, not_7_out, not_8_out,
       not_9_out, not_10_out, not_11_out, not_12_out, not_13_out, not_14_out, not_15_out, not_16_out,
       not_17_out, not_18_out, not_19_out, not_20_out;

  not not_1 (not_1_out, x5);
  not not_2 (not_2_out, x4);
  not not_3 (not_3_out, x5);
  not not_4 (not_4_out, x3);
  not not_5 (not_5_out, x5);
  not not_6 (not_6_out, x2);
  not not_7 (not_7_out, x5);
  not not_8 (not_8_out, x1);
  not not_9 (not_9_out, x4);
  not not_10 (not_10_out, x3);
  not not_11 (not_11_out, x4);
  not not_12 (not_12_out, x2);
  not not_13 (not_13_out, x4);
  not not_14 (not_14_out, x1);
  not not_15 (not_15_out, x3);
  not not_16 (not_16_out, x2);
  not not_17 (not_17_out, x3);
  not not_18 (not_18_out, x1);
  not not_19 (not_19_out, x2);
  not not_20 (not_20_out, x1);
  and and_1 (and_1_out, not_1_out, not_2_out, x3, x2, x1);
  and and_2 (and_2_out, not_3_out, x4, not_4_out, x2, x1);
  and and_3 (and_3_out, not_5_out, x4, x3, not_6_out, x1);
  and and_4 (and_4_out, not_7_out, x4, x3, x2, not_8_out);
  and and_5 (and_5_out, x5, not_9_out, not_10_out, x2, x1);
  and and_6 (and_6_out, x5, not_11_out, x3, not_12_out, x1);
  and and_7 (and_7_out, x5, not_13_out, x3, x2, not_14_out);
  and and_8 (and_8_out, x5, x4, not_15_out, not_16_out, x1);
  and and_9 (and_9_out, x5, x4, not_17_out, x2, not_18_out);
  and and_10 (and_10_out, x5, x4, x3, not_19_out, not_20_out);
  or or_1 (y, and_1_out, and_2_out, and_3_out, and_4_out, and_5_out, and_6_out, and_7_out, and_8_out, and_9_out, and_10_out);
endmodule

module _2 (
  input  x3,
  input  x2,
  input  x1,
  output y
);

  wire and_1_out, and_2_out, and_3_out, nand_1_out, nor_1_out, nor_2_out, not_1_out;

  not not_1 (not_1_out, x2);
  and and_1 (and_1_out, not_1_out, x1);
  nor nor_1 (nor_1_out, and_1_out, x2);
  nand nand_1 (nand_1_out, x3, x1);
  and and_2 (and_2_out, x3, nor_1_out);
  and and_3 (and_3_out, x3, x2, x1);
  nor nor_2 (nor_2_out, nand_1_out, and_2_out);
  or or_1 (y, and_3_out, nor_2_out);
endmodule

module _3 (
  input  x4,
  input  x3,
  input  x2,
  input  x1,
  output y
);

  wire and_1_out, and_2_out, and_3_out, and_4_out, and_5_out, and_6_out, and_7_out, and_8_out, not_1_out,
       not_2_out, not_3_out, not_4_out, not_5_out, not_6_out, not_7_out, not_8_out, not_9_out, not_10_out,
       not_11_out, not_12_out;

  not not_1 (not_1_out, x3);
  not not_2 (not_2_out, x4);
  not not_3 (not_3_out, x2);
  not not_4 (not_4_out, x1);
  not not_5 (not_5_out, x2);
  not not_6 (not_6_out, x1);
  not not_7 (not_7_out, x2);
  not not_8 (not_8_out, x3);
  not not_9 (not_9_out, x4);
  not not_10 (not_10_out, x1);
  not not_11 (not_11_out, x4);
  not not_12 (not_12_out, x2);
  and and_1 (and_1_out, not_1_out, x2);
  and and_2 (and_2_out, not_2_out, x3, not_3_out, not_4_out);
  and and_3 (and_3_out, x4, not_5_out, x1);
  and and_4 (and_4_out, x4, x2, not_6_out);
  and and_5 (and_5_out, x3, not_7_out);
  and and_6 (and_6_out, x4, not_8_out, x2, x1);
  and and_7 (and_7_out, not_9_out, x2, not_10_out);
  and and_8 (and_8_out, not_11_out, not_12_out, x1);
  or or_1 (y, and_1_out, and_2_out, and_3_out, and_4_out, and_5_out, and_6_out, and_7_out, and_8_out);
endmodule
