// Logisim project 2.circ as structural Verilog: 4 circuits, main circuit 1
module _1 (
  input  x1,
  input  x0,
  output y3,
  output y2,
  output y1,
  output y0
);

  wire not_1_out, not_2_out, not_3_out, not_4_out;

  not not_1 (not_1_out, x1);
  not not_2 (not_2_out, x0);
  not not_3 (not_3_out, x1);
  not not_4 (not_4_out, x0);
  nor nor_1 (y3, not_1_out, not_2_out);
  nor nor_2 (y2, not_3_out, x0);
  nor nor_3 (y1, x1, not_4_out);
  nor nor_4 (y0, x1, x0);
endmodule

module _3 (
  input  x3,
  input  x2,
  input  x1,
  output y
);

  wire decoder_1_out1, decoder_1_out3, decoder_1_out7;

  Decoder #(.select(3)) decoder_1 (
    .out1(decoder_1_out1), .out3(decoder_1_out3), .out7(decoder_1_out7), .sel({x1, x2, x3}));  // open: out0, out2, out4, out5, out6, en
  or or_1 (y, decoder_1_out1, decoder_1_out3, decoder_1_out7);
endmodule

module _2 (
  input  x0,
  input  x1,
  input  x2,
  input  in_4,
  input  x3,
  input  x4,
  input  x5,
  output y0,
  output y1,
  output y2,
  output y3,
  output y4,
  output y5,
  output y6,
  output y7,
  output y8,
  output y9,
  output y10,
  output y11,
  output y12,
  output y13,
  output y14,
  output y15,
  output y16,
  output y17,
  output y18,
  output y19,
  output y20,
  output y21,
  output y22,
  output y23
);

  wire decoder_1_out0, decoder_1_out1, decoder_1_out2;

  Decoder #(.select(3)) decoder_1 (
    .out0(decoder_1_out0), .out1(decoder_1_out1), .out2(decoder_1_out2), .sel({x5, x4, x3}), .en(in_4));  // open: out3, out4, out5, out6, out7
  Decoder #(.select(3)) decoder_2 (
    .out0(y0), .out1(y1), .out2(y2), .out3(y3), .out4(y4), .out5(y5), .out6(y6), .out7(y7),
    .sel({x2, x1, x0}), .en(decoder_1_out0));
  Decoder #(.select(3)) decoder_3 (
    .out0(y8), .out1(y9), .out2(y10), .out3(y11), .out4(y12), .out5(y13), .out6(y14), .out7(y15),
    .sel({x2, x1, x0}), .en(decoder_1_out1));
  Decoder #(.select(3)) decoder_4 (
    .out0(y16), .out1(y17), .out2(y18), .out3(y19), .out4(y20), .out5(y21), .out6(y22), .out7(y23),
    .sel({x2, x1, x0}), .en(decoder_1_out2));
endmodule

module _4 (
  input  x15,
  input  x14,
  input  x13,
  input  x12,
  input  x11,
  input  x10,
  input  x9,
  input  x8,
  input  x7,
  input  x6,
  input  x5,
  input  x4,
  input  x3,
  input  x2,
  input  x1,
  input  x0,
  output y0,
  output y1,
  output y2,
  output y3
);

  or or_1 (y0, x15, x14, x13, x12, x11, x10, x9, x8);
  or or_2 (y1, x15, x14, x13, x12, x7, x6, x5, x4);
  or or_3 (y2, x15, x14, x11, x10, x7, x6, x3, x2);
  or or_4 (y3, x15, x13, x11, x9, x7, x5, x3, x1);
endmodule
