// Logisim project 3.1.circ as structural Verilog: 1 circuit, main circuit main
module main (
  input  x0,
  input  x1,
  input  x2,
  input  x3,
  input  y0,
  input  y1,
  input  y2,
  input  y3,
  output F1_F2
);

  wire xnor_1_out, xnor_2_out, xnor_3_out, xnor_4_out;

  xnor xnor_1 (xnor_1_out, x0, y0);
  xnor xnor_2 (xnor_2_out, x1, y1);
  xnor xnor_3 (xnor_3_out, y3, x3);
  xnor xnor_4 (xnor_4_out, x2, y2);
  and and_1 (F1_F2, xnor_1_out, xnor_2_out, xnor_3_out, xnor_4_out);

  // Notes on the sheet:
  //   x0
  //   x1
  //   x2
  //   X3
  //   y0
  //   y1
  //   y2
  //   y3
endmodule
