// Logisim project 3.2.circ as structural Verilog: 1 circuit, main circuit main
module main (
  input  x0,
  input  x1,
  input  y0,
  input  y1,
  output Fy_Fx,
  output Fy_Fx_2,
  output Fx_Fy
);

  wire and_1_out, and_2_out, not_1_out, not_2_out, not_3_out, not_4_out, xnor_1_out, xnor_2_out;

  not not_1 (not_1_out, x0);
  not not_2 (not_2_out, x1);
  not not_3 (not_3_out, y0);
  not not_4 (not_4_out, y1);
  and and_1 (and_1_out, x0, not_3_out, xnor_2_out);
  and and_2 (and_2_out, not_4_out, x1);
  xnor xnor_1 (xnor_1_out, x0, y0);
  xnor xnor_2 (xnor_2_out, x1, y1);
  or or_1 (Fy_Fx, and_1_out, and_2_out);
  and and_3 (Fx_Fy, xnor_2_out, xnor_1_out);
  xnor xnor_3 (Fy_Fx_2, Fy_Fx, Fx_Fy);

  // Notes on the sheet:
  //   x0
  //   ~x0
  //   x1
  //   ~x1
  //   y0
  //   ~y0
  //   y1
  //   ~y1
endmodule
