// Logisim project 3.3.circ as structural Verilog: 1 circuit, main circuit main
module main (
  input  A,
  input  in_2,
  input  B,
  input  in_4,
  input  C,
  input  in_6,
  input  D,
  input  in_8,
  output A_2,
  output B_2,
  output C_2,
  output D_2
);

  wire main_1_fy_fx, main_1_fy_fx_2, main_2_fy_fx, main_2_fy_fx_2, main_3_fy_fx, main_3_fy_fx_2,
       main_4_fy_fx, main_4_fy_fx_2, main_5_fy_fx, main_5_fy_fx_2, main_6_fy_fx, main_6_fy_fx_2;

  _3_2_main main_1 (
    .x0(A), .x1(in_2), .y0(B), .y1(in_4), .Fy_Fx(main_1_fy_fx), .Fy_Fx_2(main_1_fy_fx_2));  // open: Fx_Fy
  _3_2_main main_2 (
    .x0(A), .x1(in_2), .y0(C), .y1(in_6), .Fy_Fx(main_2_fy_fx), .Fy_Fx_2(main_2_fy_fx_2));  // open: Fx_Fy
  _3_2_main main_3 (
    .x0(A), .x1(in_2), .y0(D), .y1(in_8), .Fy_Fx(main_3_fy_fx), .Fy_Fx_2(main_3_fy_fx_2));  // open: Fx_Fy
  _3_2_main main_4 (
    .x0(B), .x1(in_4), .y0(C), .y1(in_6), .Fy_Fx(main_4_fy_fx), .Fy_Fx_2(main_4_fy_fx_2));  // open: Fx_Fy
  _3_2_main main_5 (
    .x0(B), .x1(in_4), .y0(D), .y1(in_8), .Fy_Fx(main_5_fy_fx), .Fy_Fx_2(main_5_fy_fx_2));  // open: Fx_Fy
  _3_2_main main_6 (
    .x0(C), .x1(in_6), .y0(D), .y1(in_8), .Fy_Fx(main_6_fy_fx), .Fy_Fx_2(main_6_fy_fx_2));  // open: Fx_Fy
  and and_1 (A_2, main_1_fy_fx, main_2_fy_fx, main_3_fy_fx);
  and and_2 (B_2, main_1_fy_fx_2, main_4_fy_fx, main_5_fy_fx);
  and and_3 (C_2, main_2_fy_fx_2, main_4_fy_fx_2, main_6_fy_fx);
  and and_4 (D_2, main_3_fy_fx_2, main_5_fy_fx_2, main_6_fy_fx_2);
endmodule
