// Logisim project 5lab.circ as structural Verilog: 3 circuits, main circuit 5.1
module _5_1 (
  input  a0,
  input  b0,
  input  a1,
  input  b1,
  input  a2,
  input  b2,
  input  a3,
  input  b3,
  output Fa_b
);

  wire xor_1_out, xor_2_out, xor_3_out, xor_4_out;

  xor xor_1 (xor_1_out, a0, b0);
  xor xor_2 (xor_2_out, a1, b1);
  xor xor_3 (xor_3_out, a2, b2);
  xor xor_4 (xor_4_out, a3, b3);
  nor nor_1 (Fa_b, xor_1_out, xor_2_out, xor_3_out, xor_4_out);
endmodule

module _5_2 (
  input  a0,
  input  a1,
  input  b0,
  input  b1,
  output Fa_b,
  output Fa_b_2,
  output Fa_b_3
);

  wire and_1_out, and_2_out, and_3_out, and_4_out, and_5_out, and_6_out, and_7_out, and_8_out, and_9_out,
       and_10_out, not_1_out, not_2_out, not_3_out, not_4_out, not_5_out, not_6_out, not_7_out, not_8_out,
       not_9_out, not_10_out, not_11_out, not_12_out, not_13_out, not_14_out, not_15_out, not_16_out;

  not not_1 (not_1_out, a0);
  not not_2 (not_2_out, a1);
  not not_3 (not_3_out, b0);
  not not_4 (not_4_out, b1);
  not not_5 (not_5_out, a0);
  not not_6 (not_6_out, b0);
  not not_7 (not_7_out, a1);
  not not_8 (not_8_out, b1);
  not not_9 (not_9_out, b0);
  not not_10 (not_10_out, b1);
  not not_11 (not_11_out, b0);
  not not_12 (not_12_out, b1);
  not not_13 (not_13_out, a0);
  not not_14 (not_14_out, a1);
  not not_15 (not_15_out, a0);
  not not_16 (not_16_out, a1);
  and and_1 (and_1_out, not_1_out, not_2_out, not_3_out, not_4_out);
  and and_2 (and_2_out, not_5_out, a1, not_6_out, b1);
  and and_3 (and_3_out, a0, not_7_out, b0, not_8_out);
  and and_4 (and_4_out, a0, a1, b0, b1);
  and and_5 (and_5_out, a1, not_9_out, not_10_out);
  and and_6 (and_6_out, a0, not_11_out);
  and and_7 (and_7_out, a0, a1, not_12_out);
  and and_8 (and_8_out, not_13_out, not_14_out, b1);
  and and_9 (and_9_out, not_15_out, b0);
  and and_10 (and_10_out, not_16_out, b0, b1);
  or or_1 (Fa_b, and_1_out, and_2_out, and_3_out, and_4_out);
  or or_2 (Fa_b_2, and_5_out, and_6_out, and_7_out);
  or or_3 (Fa_b_3, and_8_out, and_9_out, and_10_out);
endmodule

module _5_3 (
  input  a0,
  input  a1,
  input  b0,
  input  b1,
  input  c0,
  input  c1,
  input  d0,
  input  d1,
  output a,
  output b,
  output c,
  output d
);

  wire n5_2_2_fa_b_2, n5_2_2_fa_b_3, n5_2_3_fa_b_2, n5_2_3_fa_b_3, n5_2_4_fa_b_2, n5_2_4_fa_b_3,
       n5_2_5_fa_b_2, n5_2_5_fa_b_3;

  _5_2 u_5_2_1 ();  // open: a0, a1, b0, b1, Fa_b, Fa_b_2, Fa_b_3
  _5_2 u_5_2_2 (.a0(a0), .a1(a1), .b0(b0), .b1(b1), .Fa_b_2(n5_2_2_fa_b_2), .Fa_b_3(n5_2_2_fa_b_3));  // open: Fa_b
  _5_2 u_5_2_3 (.a0(b0), .a1(b1), .b0(c0), .b1(c1), .Fa_b_2(n5_2_3_fa_b_2), .Fa_b_3(n5_2_3_fa_b_3));  // open: Fa_b
  _5_2 u_5_2_4 (.a0(c0), .a1(c1), .b0(d0), .b1(d1), .Fa_b_2(n5_2_4_fa_b_2), .Fa_b_3(n5_2_4_fa_b_3));  // open: Fa_b
  _5_2 u_5_2_5 (.a0(a0), .a1(a1), .b0(d0), .b1(d1), .Fa_b_2(n5_2_5_fa_b_2), .Fa_b_3(n5_2_5_fa_b_3));  // open: Fa_b
  and and_1 (a, n5_2_2_fa_b_2, n5_2_5_fa_b_2);
  and and_2 (b, n5_2_2_fa_b_3, n5_2_3_fa_b_2);
  and and_3 (c, n5_2_3_fa_b_3, n5_2_4_fa_b_2);
  and and_4 (d, n5_2_4_fa_b_3, n5_2_5_fa_b_3);

  // Notes on the sheet:
  //   d1
  //   c1
  //   d0
  //   b1
  //   c0
  //   a1
  //   b0
  //   a0
endmodule
