// Logisim project LAB11.Naumik(1v).circ as structural Verilog: 2 circuits, main circuit 1
module _1 (
  input  [7:0] D,
  input  [2:0] A,
  output [7:0] D_2
);

  wire clock_1_out, demultiplexer_1_out0, demultiplexer_1_out1, demultiplexer_1_out2, demultiplexer_1_out3,
       demultiplexer_1_out4, demultiplexer_1_out5, demultiplexer_1_out6, demultiplexer_1_out7;
  wire [7:0] register_1_q, register_2_q, register_3_q, register_4_q, register_5_q, register_6_q,
       register_7_q, register_8_q;

  Demultiplexer #(.select(3)) demultiplexer_1 (
    .out0(demultiplexer_1_out0), .out1(demultiplexer_1_out1), .out2(demultiplexer_1_out2),
    .out3(demultiplexer_1_out3), .out4(demultiplexer_1_out4), .out5(demultiplexer_1_out5),
    .out6(demultiplexer_1_out6), .out7(demultiplexer_1_out7), .in(clock_1_out), .sel(A));  // open: en
  Clock clock_1 (.out(clock_1_out));
  Register register_1 (.D(D), .Q(register_1_q), .clk(demultiplexer_1_out0));  // open: en, clr
  Register register_2 (.D(D), .Q(register_2_q), .clk(demultiplexer_1_out1));  // open: en, clr
  Register register_3 (.D(D), .Q(register_3_q), .clk(demultiplexer_1_out2));  // open: en, clr
  Register register_4 (.D(D), .Q(register_4_q), .clr(demultiplexer_1_out3));  // open: en, clk
  Register register_5 (.D(D), .Q(register_5_q), .clk(demultiplexer_1_out4));  // open: en, clr
  Register register_6 (.D(D), .Q(register_6_q), .clk(demultiplexer_1_out5));  // open: en, clr
  Register register_7 (.D(D), .Q(register_7_q), .clk(demultiplexer_1_out6));  // open: en, clr
  Register register_8 (.D(D), .Q(register_8_q), .clk(demultiplexer_1_out7));  // open: en, clr
  Multiplexer #(.select(3), .width(8)) multiplexer_1 (
    .in0(register_1_q), .in1(register_2_q), .in2(register_3_q), .in3(register_4_q), .in4(register_5_q),
    .in5(register_6_q), .in6(register_7_q), .in7(register_8_q), .out(D_2), .sel(A));  // open: en
endmodule

module _2 (
);

  wire and_1_out, clock_1_out, not_1_out;
  wire [1:0] ram_1_data;
  wire [2:0] counter_1_q;
  wire [7:0] adder_1_out, ram_2_data, register_1_q;

  Clock clock_1 (.out(clock_1_out));
  Counter #(.width(3), .max('h7)) counter_1 (.Q(counter_1_q), .clk(clock_1_out));  // open: load, D, count, carry, clr
  not not_1 (not_1_out, clock_1_out);
  RAM #(.addrWidth(3), .dataWidth(2), .bus("separate")) ram_1 (
    .addr(counter_1_q), .data(ram_1_data));  // open: din, str, sel, clk, ld, clr
  RAM #(.addrWidth(3), .bus("separate")) ram_2 (
    .addr(counter_1_q), .din(register_1_q), .data(ram_2_data), .clk(ram_1_data[1]));  // open: str, sel, ld, clr
  Adder adder_1 (.a(register_1_q), .b(ram_2_data), .out(adder_1_out));  // open: cin, cout
  and and_1 (and_1_out, ram_1_data[0], not_1_out);
  Register register_1 (.D(adder_1_out), .Q(register_1_q), .clk(and_1_out));  // open: en, clr
endmodule
