// Logisim project Naumik13.1.circ as structural Verilog: 3 circuits, main circuit 2
module _2 (
  input  x3,
  input  x2,
  input  x1,
  output y
);

  wire and_1_out, and_2_out, and_3_out, nand_1_out, nor_1_out, not_1_out, not_2_out;

  not not_1 (not_1_out, x2);
  not not_2 (not_2_out, x1);
  and and_1 (and_1_out, not_1_out, x1);
  and and_2 (and_2_out, x3, not_2_out);
  nor nor_1 (nor_1_out, and_1_out, and_2_out);
  nand nand_1 (nand_1_out, x3, x2, x1);
  and and_3 (and_3_out, x3, nor_1_out);
  nor nor_2 (y, nand_1_out, and_3_out);

  // Notes on the sheet:
  //   Naumik Serhii
endmodule

module _1 (
  input  x5,
  input  x4,
  input  x3,
  input  x2,
  input  x1,
  output y
);

  wire and_1_out, and_2_out, and_3_out, and_4_out, and_5_out;

  and and_1 (and_1_out, x4, x3, x2, x1);
  and and_2 (and_2_out, x5, x3, x2, x1);
  and and_3 (and_3_out, x5, x4, x2, x1);
  and and_4 (and_4_out, x5, x4, x3, x1);
  and and_5 (and_5_out, x5, x4, x3, x2);
  or or_1 (y, and_1_out, and_2_out, and_3_out, and_4_out, and_5_out);

  // Notes on the sheet:
  //   Naumik Serhii
endmodule

module _3 (
  input  x4,
  input  x3,
  input  x2,
  input  x1,
  output y
);

  wire and_1_out, and_2_out, and_3_out, and_4_out, and_5_out, and_6_out, not_1_out, not_2_out, not_3_out,
       not_4_out, not_5_out, not_6_out, not_7_out, not_8_out, not_9_out, not_10_out;

  not not_1 (not_1_out, x4);
  not not_2 (not_2_out, x2);
  and and_1 (and_1_out, not_1_out, not_2_out, not_3_out);
  not not_3 (not_3_out, x1);
  not not_4 (not_4_out, x4);
  not not_5 (not_5_out, x3);
  and and_2 (and_2_out, not_4_out, not_5_out, x2);
  not not_6 (not_6_out, x3);
  and and_3 (and_3_out, not_6_out, x2, not_7_out);
  not not_7 (not_7_out, x1);
  not not_8 (not_8_out, x4);
  and and_4 (and_4_out, not_8_out, x3, not_9_out);
  not not_9 (not_9_out, x2);
  not not_10 (not_10_out, x2);
  and and_5 (and_5_out, x4, not_10_out, x1);
  and and_6 (and_6_out, x4, x3, x1);
  or or_1 (y, and_1_out, and_2_out, and_3_out, and_4_out, and_5_out, and_6_out);

  // Notes on the sheet:
  //   Naumik Serhii
endmodule
