// Logisim project Наумік10.circ as structural Verilog: 3 circuits, main circuit main
module main (
  input  \С 
);

  wire j_k_ff_1_qn, j_k_ff_2_qn, j_k_ff_3_qn, j_k_ff_4_qn, j_k_ff_5_qn, not_1_out, not_2_out, not_3_out,
       not_4_out, not_5_out, undriven, undriven_2;
  wire [0:0] j_k_ff_5_q;
  wire [3:0] j_k_ff_1_q;

  J_K_Flip_Flop j_k_ff_1 (
    .J(j_k_ff_1_qn), .clk(\С ), .K(not_1_out), .Q(j_k_ff_1_q[0]), .Qn(j_k_ff_1_qn));  // open: preset, en, reset
  not not_1 (not_1_out, j_k_ff_1_qn);
  not not_2 (not_2_out, j_k_ff_2_qn);
  J_K_Flip_Flop j_k_ff_2 (
    .J(j_k_ff_2_qn), .clk(j_k_ff_1_q[0]), .K(not_2_out), .Q(j_k_ff_1_q[1]), .Qn(j_k_ff_2_qn));  // open: preset, en, reset
  not not_3 (not_3_out, j_k_ff_3_qn);
  J_K_Flip_Flop j_k_ff_3 (
    .J(j_k_ff_3_qn), .clk(j_k_ff_1_q[1]), .K(not_3_out), .Q(j_k_ff_1_q[2]), .Qn(j_k_ff_3_qn), .reset(undriven));  // open: preset, en
  J_K_Flip_Flop j_k_ff_4 (
    .J(j_k_ff_4_qn), .clk(j_k_ff_1_q[2]), .K(not_4_out), .Q(j_k_ff_1_q[3]), .Qn(j_k_ff_4_qn));  // open: preset, en, reset
  not not_4 (not_4_out, j_k_ff_4_qn);
  Hex_Digit_Display hex_digit_display_1 (.value({3'b000, j_k_ff_5_q[0]}));  // open: dp
  not not_5 (not_5_out, j_k_ff_5_qn);
  Hex_Digit_Display hex_digit_display_2 (.value(j_k_ff_1_q));  // open: dp
  J_K_Flip_Flop j_k_ff_5 (
    .J(j_k_ff_5_qn), .clk(j_k_ff_1_q[3]), .K(not_5_out), .Q(j_k_ff_5_q[0]), .Qn(j_k_ff_5_qn),
    .preset(undriven_2));  // open: en, reset
endmodule

module _1 (
  input  \С 
);

  wire d_ff_1_qn, d_ff_2_qn, d_ff_3_qn, d_ff_4_qn;
  wire [3:0] d_ff_1_q;

  D_Flip_Flop d_ff_1 (.clk(\С ), .D(d_ff_1_qn), .Q(d_ff_1_q[0]), .Qn(d_ff_1_qn));  // open: preset, en, reset
  D_Flip_Flop d_ff_2 (.clk(d_ff_1_q[0]), .D(d_ff_2_qn), .Q(d_ff_1_q[1]), .Qn(d_ff_2_qn));  // open: preset, en, reset
  D_Flip_Flop d_ff_3 (.clk(d_ff_1_q[1]), .D(d_ff_3_qn), .Q(d_ff_1_q[2]), .Qn(d_ff_3_qn));  // open: preset, en, reset
  D_Flip_Flop d_ff_4 (.clk(d_ff_1_q[2]), .D(d_ff_4_qn), .Q(d_ff_1_q[3]), .Qn(d_ff_4_qn));  // open: preset, en, reset
  Hex_Digit_Display hex_digit_display_1 (.value(d_ff_1_q));  // open: dp
endmodule

module _2 (
  input  \С 
);

  wire nand_1_out, nand_2_out, nand_3_out;
  wire [3:0] t_ff_1_q;

  T_Flip_Flop t_ff_1 (.clk(\С ), .T(1'b1), .Q(t_ff_1_q[0]));  // open: Qn, preset, reset, en
  nand nand_1 (nand_1_out, t_ff_1_q[0], \С );
  nand nand_2 (nand_2_out, t_ff_1_q[0], t_ff_1_q[1], \С );
  T_Flip_Flop t_ff_2 (.clk(nand_1_out), .T(1'b1), .Q(t_ff_1_q[1]));  // open: Qn, preset, reset, en
  T_Flip_Flop t_ff_3 (.clk(nand_2_out), .T(1'b1), .Q(t_ff_1_q[2]));  // open: Qn, preset, reset, en
  nand nand_3 (nand_3_out, t_ff_1_q[1], t_ff_1_q[0], t_ff_1_q[2], \С );
  T_Flip_Flop t_ff_4 (.clk(nand_3_out), .T(1'b1), .Q(t_ff_1_q[3]));  // open: Qn, preset, reset, en
  Hex_Digit_Display hex_digit_display_1 (.value(t_ff_1_q));  // open: dp
endmodule
